# Fritzing sketch Home Controller pakai Telegram (saved by Fritzing 0.9.5d)
circuit board: 8.46667cm x 5.64444cm
breadboards: 1

parts:
  Stepdown_(LM2596) = RioRand LM2596
  Relay_Pompa_Air = RELAY [package=OJ]
  Relay_Lampu = RELAY [package=OJ]
  Tansistor_NPN = NPN-Transistor [package="TO92 [THT]"]
  R1 = Resistor [tolerance=±5% resistance=220 package="1206 [SMD]"]
  Power = Power Jack [package=power_jack_pth_lock]
  Buzzer = Piezo Speaker
  WeMos_D1_Mini1 = WeMos D1 Mini
  Dioda = Rectifier Diode [part_number=1N4001 package="300 mil [THT]"]
  Led_Pompa = LTE-302 [package=lte-302]
  Led_Lampu = LTE-302 [package=lte-302]
  R2 = Resistor [tolerance=±5% resistance=220 package="1206 [SMD]"]

nets:
  N1: Stepdown_(LM2596).Pin_1, Power.GND
  N2: Stepdown_(LM2596).Pin_2, Power.PWR, Dioda.cathode, Dioda.anode
  N3: Stepdown_(LM2596).Pin_3, Buzzer.pin2, WeMos_D1_Mini1.5V
  N4: Stepdown_(LM2596).Pin_4, Relay_Pompa_Air.COIL2, Relay_Lampu.COIL2, Tansistor_NPN.E, WeMos_D1_Mini1.G, R2.Pin_1
  N5: Relay_Pompa_Air.COIL1, WeMos_D1_Mini1.D4
  N6: Relay_Lampu.COIL1, WeMos_D1_Mini1.D3
  N7: Tansistor_NPN.B, R1.Pin_1
  N8: Tansistor_NPN.C, Buzzer.pin1
  N9: R1.Pin_0, WeMos_D1_Mini1.D8
  N10: WeMos_D1_Mini1.D6, Led_Pompa.A
  N11: WeMos_D1_Mini1.D7, Led_Lampu.A
  N12: Led_Pompa.C, Led_Lampu.C, R2.Pin_0

// code stored in the sketch: Code Kontroller Telegram.ino
#include "CTBot.h"


CTBot myBot;


String ssid = "DELLA";
String pass = "della2000";
String token = "6823105395:AAHupWkFr7ra8UuQ3uOrvluA0h770xJ-QZc";



int relayLampu = 0;   //Lampu - Pin D3  ==> BIRUs
int relayPompaAir = 2;   // Pompa Air - Pin D4  ==> HIJAU
int ledrelayLampu = 13; //OK - Pin D7
int ledrelayPompaAir = 12; //OK - Pin D6  
int buzzer = 15;  //OK - Pin D8
                  


void setup() {
  // initialize the Serial
  Serial.begin(115200);
  Serial.println("Starting TelegramBot...");


  // connect the ESP8266 to the desired access point
  myBot.wifiConnect(ssid, pass);
  // set the telegram bot token
  myBot.setTelegramToken(token);


  pinMode(relayLampu, OUTPUT_OPEN_DRAIN);
  pinMode(relayPompaAir, OUTPUT_OPEN_DRAIN);
  digitalWrite(relayLampu, HIGH);           //Relay Normally Close (NC)
  digitalWrite(relayPompaAir, HIGH);           //Relay Normally Close (NC)


  pinMode(ledrelayLampu, OUTPUT || INPUT);
  pinMode(ledrelayPompaAir, OUTPUT || INPUT);
  digitalWrite(ledrelayLampu, LOW);          
  digitalWrite(ledrelayPompaAir, LOW);      


  pinMode(buzzer, OUTPUT);


  // check if all things are ok
  if (myBot.testConnection()){
    Serial.println("\ntestConnection OK!");
    }
  else{
    Serial.println("\ntestConnection GAGAL!");
  }


}



void loop() {
     
  // a variable to store telegram message data
  TBMessage msg;


  // if there is an incoming message...
  if (myBot.getNewMessage(msg)) {
    if (msg.text.equalsIgnoreCase("/pompaOn")) 
    { 
      digitalWrite(relayPompaAir, LOW);  
      myBot.sendMessage(msg.sender.id, "Pompa Air Dihidupkan!");
      digitalWrite(ledrelayPompaAir, HIGH);
      beepHidup(); 
    }
    else if (msg.text.equalsIgnoreCase("/pompaOff")) 
    {             
      digitalWrite(relayPompaAir, HIGH);                            
      myBot.sendMessage(msg.sender.id, "Pompa Air Dimatikan!"); 
      digitalWrite(ledrelayPompaAir, LOW);
      beepMati(); 
    }
    else if (msg.text.equalsIgnoreCase("/lampuOff")) 
    {             
      digitalWrite(relayLampu, HIGH);                            
      myBot.sendMessage(msg.sender.id, "Lampu Dimatikan!"); 
      digitalWrite(ledrelayLampu, LOW);
      beepMati(); 
    }
    else if (msg.text.equalsIgnoreCase("/lampuOn")) 
    { 
      digitalWrite(relayLampu, LOW);  
      myBot.sendMessage(msg.sender.id, "Lampu Dihidupkan!");
      digitalWrite(ledrelayLampu, HIGH);
      beepHidup(); 
    }
    else if (msg.text.equalsIgnoreCase("/allOn")) 
    {             
      digitalWrite(relayPompaAir, LOW);
      digitalWrite(relayLampu, LOW);                            
      myBot.sendMessage(msg.sender.id, "Pompa Air dan Lampu Dihidupkan!"); 
      digitalWrite(ledrelayPompaAir, HIGH);
      digitalWrite(ledrelayLampu, HIGH);
      beepHidup(); 
    }
    else if (msg.text.equalsIgnoreCase("/allOff")) 
    {             
      digitalWrite(relayPompaAir, HIGH);
      digitalWrite(relayLampu, HIGH);                            
      myBot.sendMessage(msg.sender.id, "Pompa Air dan Lampu Dimatikan!"); 
      digitalWrite(ledrelayPompaAir, LOW);
      digitalWrite(ledrelayLampu, LOW);
      beepMati(); 
    }
    else if (msg.text.equalsIgnoreCase("/status")) 
      {     
          if(digitalRead(ledrelayLampu) == HIGH && digitalRead(ledrelayPompaAir) == HIGH){
          myBot.sendMessage(msg.sender.id, "Pompa Air dan Lampu Masih Hidup!");
          }  
          else if (digitalRead(ledrelayLampu) == LOW && digitalRead(ledrelayPompaAir) == LOW){
          myBot.sendMessage(msg.sender.id, "Pompa Air dan Lampu Telah Mati!");
          }
          else if (digitalRead(ledrelayLampu) == HIGH && digitalRead(ledrelayPompaAir) == LOW){
          myBot.sendMessage(msg.sender.id, "Pompa Air Mati dan Lampu Hidup!");
          }
          else if (digitalRead(ledrelayLampu) == LOW && digitalRead(ledrelayPompaAir) == HIGH){
          myBot.sendMessage(msg.sender.id, "Pompa Air Hidup dan Lampu Mati!");
          }
      }
    else if (msg.text.equalsIgnoreCase("/start")){                                                   
      // generate the message for the sender
      String reply1;
            reply1 = "Hallo >>" + msg.sender.username + "<<.\n";
            reply1 += "Klik perintah tanda biru dibawah \n";
            reply1 += "/status    : cek status Listrik\n";
            reply1 += "/pompaOn   : Menyalakan Pompa Air\n";
            reply1 += "/pompaOff  : Mematikan Pompa Air\n";
            reply1 += "/lampuOn   : Menyalakan Lampu\n";
            reply1 += "/lampuOff  : Mematikan Lampu\n";
            reply1 += "/allOn     : Menyalakan Semua Listrik\n";
            reply1 += "/allOff    : Mematikan Semua listrik\n";
      myBot.sendMessage(msg.sender.id, reply1);             
    }
    else{
      String reply2;
            reply2 = "Perintah Salah "+ msg.sender.username + " !\n";
            reply2 += "Coba lagi dengan perintah yang benar!\n";
      myBot.sendMessage(msg.sender.id, reply2);
    }
   
  }
  // wait 500 milliseconds
  delay(500);
}


void beepHidup (){
  digitalWrite(buzzer, HIGH);
  delay(1000);
  digitalWrite(buzzer, LOW);
}


void beepMati (){
  digitalWrite(buzzer, HIGH);
  delay(250);
  digitalWrite(buzzer, LOW);
  delay(50);
  digitalWrite(buzzer, HIGH);
  delay(250);
  digitalWrite(buzzer, LOW);
}
